# Fritzing sketch fritzing (saved by Fritzing 0.9.2b)
breadboards: 3

parts:
  Part1 = Arduino Uno (Rev3)
  Part3 = Sonar Ultrasonic Rangefinder
  Part4 = Sonar Ultrasonic Rangefinder
  Part5 = Sonar Ultrasonic Rangefinder
  Part6 = Sonar Ultrasonic Rangefinder
  Part7 = Sonar Ultrasonic Rangefinder
  Part10 = Bluetooth HC-05 Macho
  LED1 = smd LED [color="Green (555nm)" package="0805 [SMD]"]
  R1 = Resistor [tolerance=±5% resistance=220 package="0402 [SMD]"]

nets:
  N1: Part1.A0, Part6.Trig, Part6.Echo
  N2: Part1.A1, Part4.Trig, Part4.Echo
  N3: Part1.A4/SDA, Part3.Trig, Part3.Echo
  N4: Part1.A5/SCL, Part7.Trig, Part7.Echo
  GND: Part1.GND, Part3.GND, Part4.GND, Part5.GND, Part6.GND, Part7.GND, Part10.GND
  N5: Part1.D2, R1.Pin_1
  N6: Part1.D3_PWM, Part10.RXD
  N7: Part1.D5_PWM, Part10.TXD
  N8: Part1.D6_PWM, Part5.Trig, Part5.Echo
  5V: Part1.5V, Part3.Sonar_Ultrasonic_Rangefinder, Part4.Sonar_Ultrasonic_Rangefinder, Part5.Sonar_Ultrasonic_Rangefinder, Part6.Sonar_Ultrasonic_Rangefinder, Part7.Sonar_Ultrasonic_Rangefinder, Part10.VCC, LED1.cathode
  N9: LED1.anode, R1.Pin_0
